# Fritzing sketch raspi-switch-led (saved by Fritzing 0.9.2b)
breadboards: 1

parts:
  Raspberry_Pi1 = Raspberry Pi 2
  R1 = Resistor [tolerance=±5% resistance=220 package=THT]
  LED2 = LED - 3mm [color="Red (633nm)" package="3 mm [THT]"]

nets:
  N1: Raspberry_Pi1.GND, LED2.cathode
  N2: Raspberry_Pi1.GPIO16, R1.Pin_1
  N3: R1.Pin_0, LED2.anode
