# Fritzing sketch temperature-fritzing-4k7-thermistor (saved by Fritzing 0.9.2b)
breadboards: 1

parts:
  R1 = Temperature Sensor (Thermistor) [thermistor_type=NTC part_number=4,7k package=THT]
  Bauteil1 = Arduino Nano (Rev3.0) (ICSP)
  R2 = Resistor [tolerance=±2% resistance=10k package="2512 [SMD]"]

nets:
  N1: R1.pin_0, Bauteil1.5V
  N2: R1.pin_1, Bauteil1.A0, R2.Pin_0
  N3: Bauteil1.GND, R2.Pin_1
